# Fritzing sketch Sketch (saved by Fritzing 0.9.2b)

parts:
  Raspberry_Pi1 = Raspberry Pi 2
  Power_plug1 = Power plug
  パーツ1 = ws2812b [package=THT]

nets:
  3V3: Raspberry_Pi1.3V3, パーツ1.VDD
  GND: Raspberry_Pi1.GND, Power_plug1.GND, パーツ1.VSS
  N1: Raspberry_Pi1.GIPO18, パーツ1.DIN
  5V: Raspberry_Pi1.5V, Power_plug1.VCC
